// Logisim project saguiLongo.circ as structural Verilog: 5 circuits, main circuit main
module main (
);

  wire Clk, memWrite, not_1_out;
  wire [7:0] adder_1_out, arithmetic_type_fu_1_result, arithmetic_type_fu_2_result,
       bancoregistradores_1_arithm_1_a, bancoregistradores_1_arithm_1_b, bancoregistradores_1_arithm_2_a,
       bancoregistradores_1_arithm_2_b, bancoregistradores_1_ctrl_a, bancoregistradores_1_ctrl_b,
       bancoregistradores_1_data_a, bancoregistradores_1_data_b, ctrl_type_fu_1_pc_out,
       data_type_fu_1_result, PC_q;

  Adder adder_1 (.a(PC_q), .b(ctrl_type_fu_1_pc_out), .out(adder_1_out), .cin(1'b0));  // open: cout
  Register PC (.D(adder_1_out), .en(1'b1), .clk(Clk), .Q(PC_q), .clr(1'b0));
  // ROM #(.line("quad")) rom_1: pin names not known; wires that end beside it: PC_q
  Clock clock_Global (.out(Clk));
  BancoRegistradores bancoregistradores_1 (
    .data_a(bancoregistradores_1_data_a), .data_b(bancoregistradores_1_data_b),
    .arithm_1_a(bancoregistradores_1_arithm_1_a), .arithm_1_b(bancoregistradores_1_arithm_1_b),
    .arithm_2_a(bancoregistradores_1_arithm_2_a), .arithm_2_b(bancoregistradores_1_arithm_2_b),
    .ctrl_a(bancoregistradores_1_ctrl_a), .ctrl_b(bancoregistradores_1_ctrl_b));  // open: WData_00, WEnabler_00, WData_01, WEnabler_01, WData_02, WEnabler_02, WData_03, WEnabler_03, clk, data_a_address, data_b_address, arithm_1_a_address, arithm_1_b_address, arithm_2_a_address, arithm_2_b_address, ctrl_a_address, ctrl_b_address
  not not_1 (not_1_out, memWrite);
  Data_type_FU data_type_fu_1 (
    .a(bancoregistradores_1_data_a), .b(bancoregistradores_1_data_b), .result(data_type_fu_1_result));  // open: selector
  Arithmetic_type_FU arithmetic_type_fu_1 (
    .a(bancoregistradores_1_arithm_1_a), .b(bancoregistradores_1_arithm_1_b),
    .result(arithmetic_type_fu_1_result));  // open: selector
  Arithmetic_type_FU arithmetic_type_fu_2 (
    .a(bancoregistradores_1_arithm_2_a), .b(bancoregistradores_1_arithm_2_b),
    .result(arithmetic_type_fu_2_result));  // open: selector
  Ctrl_type_FU ctrl_type_fu_1 (
    .a(bancoregistradores_1_ctrl_a), .b(bancoregistradores_1_ctrl_b), .PC_in(PC_q),
    .PC_out(ctrl_type_fu_1_pc_out));  // open: selector
  RAM #(.asyncread("true")) ram_1 (
    .addr(bancoregistradores_1_data_a), .we(memWrite), .oe(not_1_out), .clk(Clk), .din(data_type_fu_1_result));  // open: dout

  // Notes on the sheet:
  //   Memoria de Instrucoes
  //   Memoria de Dados
endmodule

module Data_type_FU (
  input  [7:0] a,
  input  [7:0] b,
  input  [1:0] selector,
  output [7:0] result
);

  wire [3:0] bit_extender_1_out;

  Bit_Extender #(.out_width(4)) bit_extender_1 (.in(b), .out(bit_extender_1_out));
  Multiplexer #(.select(2), .width(8)) multiplexer_1 (
    .in0({bit_extender_1_out, a[3:0]}), .in1({a[7:4], bit_extender_1_out}), .in2(b), .in3({8{1'b0}}),
    .out(result), .sel(selector));

  // Notes on the sheet:
  //   Move High
  //   Move Low
  //   Ld/St address
endmodule

module Ctrl_type_FU (
  input  [7:0] a,
  input  [7:0] b,
  input  [7:0] PC_in,
  input  [1:0] selector,
  output [7:0] PC_out
);

  wire isZero;
  wire [7:0] adder_1_out, multiplexer_1_out, multiplexer_2_out;

  nor nor_1 (isZero, a[0], a[1], a[2], a[3], a[5], a[6], a[7], a[4]);
  Adder adder_1 (.a(b), .b(PC_in), .out(adder_1_out), .cin(1'b0));  // open: cout
  Multiplexer #(.width(8)) multiplexer_1 (.in0(PC_in), .in1(b), .out(multiplexer_1_out), .sel(isZero));
  Multiplexer #(.width(8)) multiplexer_2 (.in0(PC_in), .in1(adder_1_out), .out(multiplexer_2_out), .sel(isZero));
  Multiplexer #(.select(2), .width(8)) multiplexer_3 (
    .in0(b), .in1(adder_1_out), .in2(multiplexer_1_out), .in3(multiplexer_2_out), .out(PC_out), .sel(selector));

  // Notes on the sheet:
  //   PC + Imm
  //   Jump Register
  //   Jump Immediate
  //   Branch On Zero Register
  //   Branch On Zero
endmodule

module Arithmetic_type_FU (
  input  [7:0] a,
  input  [7:0] b,
  input  [2:0] selector,
  output [7:0] result
);

  wire or_2_out;
  wire [7:0] adder_1_out, and_1_out, multiplexer_1_out, multiplexer_2_out, not_1_out, or_1_out,
       shifter_1_out, shifter_2_out, subtractor_1_out;

  Adder adder_1 (.a(a), .b(b), .out(adder_1_out), .cin(1'b0));  // open: cout
  Subtractor subtractor_1 (.a(a), .b(b), .out(subtractor_1_out), .bin(1'b0));  // open: bout
  assign and_1_out = a & b;  // AND_Gate and_1, 8 bits wide
  assign or_1_out = a | b;  // OR_Gate or_1, 8 bits wide
  assign not_1_out = ~b;  // NOT_Gate not_1, 8 bits wide
  Shifter shifter_1 (.in(a), .\dist (b[2:0]), .out(shifter_1_out));
  Shifter #(.shift("lr")) shifter_2 (.in(a), .\dist (b[2:0]), .out(shifter_2_out));
  Multiplexer #(.width(8)) multiplexer_1 (
    .in0(shifter_1_out), .in1({8{1'b0}}), .out(multiplexer_1_out), .sel(or_2_out));
  Multiplexer #(.width(8)) multiplexer_2 (
    .in0(shifter_2_out), .in1({8{1'b0}}), .out(multiplexer_2_out), .sel(or_2_out));
  or or_2 (or_2_out, b[7], b[6], b[5], b[4], b[3]);
  Multiplexer #(.select(3), .width(8)) multiplexer_3 (
    .in0(adder_1_out), .in1(subtractor_1_out), .in2(and_1_out), .in3(or_1_out), .in4(not_1_out),
    .in5(multiplexer_1_out), .in6(multiplexer_2_out), .in7({8{1'b0}}), .out(result), .sel(selector));

  // Notes on the sheet:
  //   Somador
  //   Subtrator
  //   And
  //   Or
  //   Not
  //   Logical Shifter Left
  //   Logical Shifter Right
endmodule

module BancoRegistradores (
  input  [7:0] WData_00,
  input  WEnabler_00,
  input  [7:0] WData_01,
  input  WEnabler_01,
  input  [7:0] WData_02,
  input  WEnabler_02,
  input  [7:0] WData_03,
  input  WEnabler_03,
  input  clk,
  input  [1:0] data_a_address,
  input  [1:0] data_b_address,
  input  [1:0] arithm_1_a_address,
  input  [1:0] arithm_1_b_address,
  input  [1:0] arithm_2_a_address,
  input  [1:0] arithm_2_b_address,
  input  [1:0] ctrl_a_address,
  input  [1:0] ctrl_b_address,
  output [7:0] data_a,
  output [7:0] data_b,
  output [7:0] arithm_1_a,
  output [7:0] arithm_1_b,
  output [7:0] arithm_2_a,
  output [7:0] arithm_2_b,
  output [7:0] ctrl_a,
  output [7:0] ctrl_b
);

  wire [1:0] undriven, undriven_2, undriven_3, undriven_4, undriven_5, undriven_6, undriven_7, undriven_8;
  wire [7:0] register_1_q, register_2_q, register_3_q, register_4_q;

  Register register_1 (.D(WData_00), .en(WEnabler_00), .Q(register_1_q), .clr(1'b0));  // open: clk
  Register register_2 (.D(WData_01), .en(WEnabler_01), .Q(register_2_q), .clr(1'b0));  // open: clk
  Register register_3 (.D(WData_02), .en(WEnabler_02), .Q(register_3_q), .clr(1'b0));  // open: clk
  Register register_4 (.D(WData_03), .en(WEnabler_03), .Q(register_4_q), .clr(1'b0));  // open: clk
  Multiplexer #(.select(2), .width(8)) multiplexer_1 (
    .in0(register_1_q), .in1(register_2_q), .in2(register_3_q), .in3(register_4_q), .out(data_a),
    .sel(undriven));
  Multiplexer #(.select(2), .width(8)) multiplexer_2 (
    .in0(register_1_q), .in1(register_2_q), .in2(register_3_q), .in3(register_4_q), .out(data_b),
    .sel(undriven_2));
  Multiplexer #(.select(2), .width(8)) multiplexer_3 (
    .in0(register_1_q), .in1(register_2_q), .in2(register_3_q), .in3(register_4_q), .out(arithm_1_a),
    .sel(undriven_3));
  Multiplexer #(.select(2), .width(8)) multiplexer_4 (
    .in0(register_1_q), .in1(register_2_q), .in2(register_3_q), .in3(register_4_q), .out(arithm_1_b),
    .sel(undriven_4));
  Multiplexer #(.select(2), .width(8)) multiplexer_5 (
    .in0(register_1_q), .in1(register_2_q), .in2(register_3_q), .in3(register_4_q), .out(arithm_2_a),
    .sel(undriven_5));
  Multiplexer #(.select(2), .width(8)) multiplexer_6 (
    .in0(register_1_q), .in1(register_2_q), .in2(register_3_q), .in3(register_4_q), .out(arithm_2_b),
    .sel(undriven_6));
  Multiplexer #(.select(2), .width(8)) multiplexer_7 (
    .in0(register_1_q), .in1(register_2_q), .in2(register_3_q), .in3(register_4_q), .out(ctrl_a),
    .sel(undriven_7));
  Multiplexer #(.select(2), .width(8)) multiplexer_8 (
    .in0(register_1_q), .in1(register_2_q), .in2(register_3_q), .in3(register_4_q), .out(ctrl_b),
    .sel(undriven_8));
endmodule
